// Logisim project P3_CPU.circ as structural Verilog: 7 circuits, main circuit main
module main (
  input  in_1,
  output [31:0] out_2,
  output [31:0] out_3,
  output out_4,
  output [4:0] out_5,
  output [31:0] out_6,
  output out_7,
  output [31:0] out_8,
  output [31:0] out_9
);

  wire clk, com_write, compare, controller_1_alu_srca, controller_1_alusrcb, controller_1_branch, imm_ext,
       not_1_out, or_1_out, PCsrc, plus_3000, RW, sign_0;
  wire [1:0] controller_1_d2r, controller_1_jump, controller_1_reg_dst, width_op;
  wire [4:0] controller_1_out_5, controller_1_out_12;
  wire [27:0] adder_1_out;
  wire [31:0] adder_2_out, adder_3_out, bit_extender_1_out, bit_extender_2_out, bit_extender_3_out,
       dm_read_1_out_5, grf_1_out_9, minus_3000, multiplexer_1_out, multiplexer_2_out, multiplexer_4_out,
       multiplexer_5_out, multiplexer_6_out, PC, ram_1_data, RD1, RegData, shifter_1_out, subtractor_1_out;
  wire [31:28] adder_1_out_2;

  Clock clock_1 (.out(clk));
  Multiplexer #(.width(32)) multiplexer_1 (
    .in0({adder_1_out_2, adder_1_out}), .in1(adder_2_out), .out(multiplexer_1_out), .sel(PCsrc));  // open: en
  Subtractor #(.width(32)) subtractor_1 (
    .a({adder_1_out_2, out_2[25:0], 2'b00}), .b(32'h3000), .out(subtractor_1_out));  // open: bin, bout
  Multiplexer #(.select(2), .width(32)) multiplexer_2 (
    .in0(multiplexer_1_out), .in1(subtractor_1_out), .in2(minus_3000), .out(multiplexer_2_out),
    .sel(controller_1_jump));  // open: in3, en
  Subtractor #(.width(32)) subtractor_2 (.a(RD1), .b(32'h3000), .out(minus_3000));  // open: bin, bout
  Register #(.width(32)) register_1 (.D(multiplexer_2_out), .Q(PC), .clk(clk), .clr(in_1));  // open: en
  not not_1 (not_1_out, com_write);
  or or_1 (or_1_out, not_1_out, compare);
  and and_1 (out_4, RW, or_1_out);
  Adder #(.width(32)) adder_1 (.a(PC), .b(32'h4), .out({adder_1_out_2, adder_1_out}));  // open: cin, cout
  ROM #(.addrWidth(12), .dataWidth(32)) rom_1 (.addr(PC[13:2]), .data(out_2), .sel(1'b1));
  Controller controller_1 (
    .in_1(out_2), .MemWrite(out_7), .Branch(controller_1_branch), .ALUsrcB(controller_1_alusrcb),
    .out_5(controller_1_out_5), .RegWrite(RW), .ALU_srcA(controller_1_alu_srca), .imm_ext(imm_ext),
    .Reg_Dst(controller_1_reg_dst), .D2R(controller_1_d2r), .jump(controller_1_jump),
    .out_12(controller_1_out_12), .compareWrite(com_write), .width_op(width_op), .sign_0(sign_0),
    .plus_3000(plus_3000));
  assign bit_extender_1_out = {{16{out_2[15]}}, out_2[15:0]};  // Bit_Extender bit_extender_1
  assign bit_extender_2_out = {{16{1'b0}}, out_2[15:0]};  // Bit_Extender bit_extender_2
  assign bit_extender_3_out = {{27{out_2[10]}}, out_2[10:6]};  // Bit_Extender bit_extender_3
  GRF grf_1 (
    .in_1(clk), .in_2(in_1), .in_3(out_4), .A1(out_2[25:21]), .A2(out_2[20:16]), .A3(out_5), .in_7(RegData),
    .out_8(RD1), .out_9(grf_1_out_9));
  Multiplexer #(.select(2), .width(5)) multiplexer_3 (
    .in0(out_2[20:16]), .in1(out_2[15:11]), .in2({5{1'b1}}), .out(out_5), .sel(controller_1_reg_dst));  // open: in3, en
  Compare compare_1 (.in_1(RD1), .in_2(grf_1_out_9), .out_4(compare), .com_op(controller_1_out_12));
  Multiplexer #(.width(32)) multiplexer_4 (
    .in0(bit_extender_1_out), .in1(bit_extender_2_out), .out(multiplexer_4_out), .sel(imm_ext));  // open: en
  Multiplexer #(.width(32)) multiplexer_5 (
    .in0(RD1), .in1(bit_extender_3_out), .out(multiplexer_5_out), .sel(controller_1_alu_srca));  // open: en
  Multiplexer #(.width(32)) multiplexer_6 (
    .in0(grf_1_out_9), .in1(multiplexer_4_out), .out(multiplexer_6_out), .sel(controller_1_alusrcb));  // open: en
  Shifter #(.width(32)) shifter_1 (.in(multiplexer_4_out), .\dist (5'b00010), .out(shifter_1_out));
  ALU alu_1 (
    .ALU_control(controller_1_out_5), .in_2(multiplexer_5_out), .in_3(multiplexer_6_out), .out_6(out_8),
    .in_5(in_1), .in_4(clk));
  DM_write dm_write_1 (.DM_data(ram_1_data), .in_2(grf_1_out_9), .op(width_op), .out_5(out_9), .Address(out_8));
  Adder #(.width(32)) adder_2 (
    .a(shifter_1_out), .b({adder_1_out_2, adder_1_out}), .out(adder_2_out));  // open: cin, cout
  and and_2 (PCsrc, controller_1_branch, compare);
  RAM #(.addrWidth(12), .dataWidth(32), .bus("separate")) ram_1 (
    .addr(out_8[13:2]), .din(out_9), .data(ram_1_data), .str(out_7), .clk(clk), .clr(in_1));  // open: sel, ld
  DM_read dm_read_1 (
    .MemData(ram_1_data), .Address(out_8), .sign_zero(sign_0), .width_op(width_op), .out_5(dm_read_1_out_5));
  Multiplexer #(.select(2), .width(32)) multiplexer_7 (
    .in0(out_8), .in1(dm_read_1_out_5), .in2({adder_1_out_2, adder_1_out}), .out(RegData),
    .sel(controller_1_d2r));  // open: in3, en
  Adder #(.width(32)) adder_3 (.a(RegData), .b(32'h3000), .out(adder_3_out));  // open: cin, cout
  Adder #(.width(32)) adder_4 (.a(PC), .b(32'h3000), .out(out_3));  // open: cin, cout
  Multiplexer #(.width(32)) multiplexer_8 (.in0(RegData), .in1(adder_3_out), .out(out_6), .sel(plus_3000));  // open: en

  // Other names for the same wires on the sheet: Instr[31:0] = out_2; MemAddr[31:0] = out_8; MemData[31:0] = out_9;
  //   MemWrite = out_7; RegAddr[4:0] = out_5; RegWrite = out_4; reset = in_1

  // Notes on the sheet:
  //   PCbranch
  //   PC+4
  //   adOfJump
  //   PC'
  //   PC
  //   PC
  //   PC+4
  //   contents of rom_1 (hex, n*v repeats v):
  //   2405ffff 4b10002 20a50002 4b10002 2402000a c 8000c04
  //   rs
  //   rt
  //   rt
  //   rd
  //   imm
  //   shamt
  //   writeReg
  //   PC+4
  //   PCbranch
  //   sign_imm
  //   zero_imm
  //   writeData
  //   SrcA
  //   SrcB
  //   ALUresult
  //   PCbranch
  //   readdata
  //   result
  //   PC+4
endmodule

module GRF (
  input  in_1,
  input  in_2,
  input  in_3,
  input  [4:0] A1,
  input  [4:0] A2,
  input  [4:0] A3,
  input  [31:0] in_7,
  output [31:0] out_8,
  output [31:0] out_9
);

  wire s1, s2, s3, s4, s5, s6, s7, s8, s9, s10, s11, s12, s13, s14, s15, s16, s17, s18, s19, s20, s21, s22,
       s23, s24, s25, s26, s27, s28, s29, s30, s31;
  wire [4:0] multiplexer_3_out;
  wire [31:0] o1, o2, o3, o4, o5, o6, o7, o8, o9, o10, o11, o12, o13, o14, o15, o16, o17, o18, o19, o20, o21,
       o22, o23, o24, o25, o26, o27, o28, o29, o30, o31;

  Multiplexer #(.select(5), .width(32)) multiplexer_1 (
    .in0({32{1'b0}}), .in1(o1), .in2(o2), .in3(o3), .in4(o4), .in5(o5), .in6(o6), .in7(o7), .in8(o8),
    .in9(o9), .in10(o10), .in11(o11), .in12(o12), .in13(o13), .in14(o14), .in15(o15), .in16(o16), .in17(o17),
    .in18(o18), .in19(o19), .in20(o20), .in21(o21), .in22(o22), .in23(o23), .in24(o24), .in25(o25),
    .in26(o26), .in27(o27), .in28(o28), .in29(o29), .in30(o30), .in31(o31), .out(out_9), .sel(A2));  // open: en
  Multiplexer #(.select(5), .width(32)) multiplexer_2 (
    .in0({32{1'b0}}), .in1(o1), .in2(o2), .in3(o3), .in4(o4), .in5(o5), .in6(o6), .in7(o7), .in8(o8),
    .in9(o9), .in10(o10), .in11(o11), .in12(o12), .in13(o13), .in14(o14), .in15(o15), .in16(o16), .in17(o17),
    .in18(o18), .in19(o19), .in20(o20), .in21(o21), .in22(o22), .in23(o23), .in24(o24), .in25(o25),
    .in26(o26), .in27(o27), .in28(o28), .in29(o29), .in30(o30), .in31(o31), .out(out_8), .sel(A1));  // open: en
  Decoder #(.select(5)) decoder_1 (
    .out1(s1), .out2(s2), .out3(s3), .out4(s4), .out5(s5), .out6(s6), .out7(s7), .out8(s8), .out9(s9),
    .out10(s10), .out11(s11), .out12(s12), .out13(s13), .out14(s14), .out15(s15), .out16(s16), .out17(s17),
    .out18(s18), .out19(s19), .out20(s20), .out21(s21), .out22(s22), .out23(s23), .out24(s24), .out25(s25),
    .out26(s26), .out27(s27), .out28(s28), .out29(s29), .out30(s30), .out31(s31), .sel(multiplexer_3_out));  // open: out0, en
  Multiplexer #(.width(5)) multiplexer_3 (.in0({5{1'b0}}), .in1(A3), .out(multiplexer_3_out), .sel(in_3));  // open: en
  Register #(.width(32)) register_1 (.D(in_7), .en(s1), .Q(o1), .clk(in_1), .clr(in_2));
  Register #(.width(32)) register_2 (.D(in_7), .en(s2), .Q(o2), .clk(in_1), .clr(in_2));
  Register #(.width(32)) register_3 (.D(in_7), .en(s3), .Q(o3), .clk(in_1), .clr(in_2));
  Register #(.width(32)) register_4 (.D(in_7), .en(s4), .Q(o4), .clk(in_1), .clr(in_2));
  Register #(.width(32)) register_5 (.D(in_7), .en(s5), .Q(o5), .clk(in_1), .clr(in_2));
  Register #(.width(32)) register_6 (.D(in_7), .en(s6), .Q(o6), .clk(in_1), .clr(in_2));
  Register #(.width(32)) register_7 (.D(in_7), .en(s7), .Q(o7), .clk(in_1), .clr(in_2));
  Register #(.width(32)) register_8 (.D(in_7), .en(s8), .Q(o8), .clk(in_1), .clr(in_2));
  Register #(.width(32)) register_9 (.D(in_7), .en(s9), .Q(o9), .clk(in_1), .clr(in_2));
  Register #(.width(32)) register_10 (.D(in_7), .en(s10), .Q(o10), .clk(in_1), .clr(in_2));
  Register #(.width(32)) register_11 (.D(in_7), .en(s11), .Q(o11), .clk(in_1), .clr(in_2));
  Register #(.width(32)) register_12 (.D(in_7), .en(s12), .Q(o12), .clk(in_1), .clr(in_2));
  Register #(.width(32)) register_13 (.D(in_7), .en(s13), .Q(o13), .clk(in_1), .clr(in_2));
  Register #(.width(32)) register_14 (.D(in_7), .en(s14), .Q(o14), .clk(in_1), .clr(in_2));
  Register #(.width(32)) register_15 (.D(in_7), .en(s15), .Q(o15), .clk(in_1), .clr(in_2));
  Register #(.width(32)) register_16 (.D(in_7), .en(s17), .Q(o17), .clk(in_1), .clr(in_2));
  Register #(.width(32)) register_17 (.D(in_7), .en(s16), .Q(o16), .clk(in_1), .clr(in_2));
  Register #(.width(32)) register_18 (.D(in_7), .en(s18), .Q(o18), .clk(in_1), .clr(in_2));
  Register #(.width(32)) register_19 (.D(in_7), .en(s19), .Q(o19), .clk(in_1), .clr(in_2));
  Register #(.width(32)) register_20 (.D(in_7), .en(s20), .Q(o20), .clk(in_1), .clr(in_2));
  Register #(.width(32)) register_21 (.D(in_7), .en(s21), .Q(o21), .clk(in_1), .clr(in_2));
  Register #(.width(32)) register_22 (.D(in_7), .en(s22), .Q(o22), .clk(in_1), .clr(in_2));
  Register #(.width(32)) register_23 (.D(in_7), .en(s23), .Q(o23), .clk(in_1), .clr(in_2));
  Register #(.width(32)) register_24 (.D(in_7), .en(s24), .Q(o24), .clk(in_1), .clr(in_2));
  Register #(.width(32)) register_25 (.D(in_7), .en(s25), .Q(o25), .clk(in_1), .clr(in_2));
  Register #(.width(32)) register_26 (.D(in_7), .en(s26), .Q(o26), .clk(in_1), .clr(in_2));
  Register #(.width(32)) register_27 (.D(in_7), .en(s27), .Q(o27), .clk(in_1), .clr(in_2));
  Register #(.width(32)) register_28 (.D(in_7), .en(s28), .Q(o28), .clk(in_1), .clr(in_2));
  Register #(.width(32)) register_29 (.D(in_7), .en(s29), .Q(o29), .clk(in_1), .clr(in_2));
  Register #(.width(32)) register_30 (.D(in_7), .en(s30), .Q(o30), .clk(in_1), .clr(in_2));
  Register #(.width(32)) register_31 (.D(in_7), .en(s31), .Q(o31), .clk(in_1), .clr(in_2));

  // Other names for the same wires on the sheet: clk = in_1; RD1[31:0] = out_8; RD2[31:0] = out_9; reset = in_2;
  //   WD[31:0] = in_7; WE = in_3
endmodule

module Controller (
  input  [31:0] in_1,
  output [1:0] D2R,
  output MemWrite,
  output Branch,
  output [4:0] out_5,
  output ALUsrcB,
  output [1:0] Reg_Dst,
  output RegWrite,
  output ALU_srcA,
  output imm_ext,
  output [1:0] jump,
  output [4:0] out_12,
  output compareWrite,
  output [1:0] width_op,
  output sign_0,
  output plus_3000
);

  wire add, addi, addiu, addu, beq, bgezal, bne, comparator_2_eq, comparator_3_eq, comparator_4_eq,
       comparator_5_eq, comparator_8_eq, comparator_9_eq, comparator_10_eq, comparator_11_eq,
       comparator_12_eq, comparator_17_eq, comparator_19_eq, comparator_20_eq, comparator_21_eq,
       comparator_22_eq, comparator_28_eq, comparator_29_eq, div, I_type, j, jal, jalr, jr, lb, lbu, lh, lhu,
       lui, lw, mfhi, mflo, mthi, mtlo, mult, ori, sb, sh, shamt, sll, sra, srl, sub, sw, write;

  Comparator #(.width(6), .mode("unsigned")) comparator_1 (
    .a(in_1[31:26]), .b({6{1'b0}}), .eq(Reg_Dst[0]));  // open: gt, lt
  Comparator #(.width(6), .mode("unsigned")) comparator_2 (
    .a(in_1[5:0]), .b(6'b100000), .eq(comparator_2_eq));  // open: gt, lt
  Comparator #(.width(6), .mode("unsigned")) comparator_3 (
    .a(in_1[5:0]), .b(6'b100010), .eq(comparator_3_eq));  // open: gt, lt
  Comparator #(.width(6), .mode("unsigned")) comparator_4 (
    .a(in_1[5:0]), .b(6'b011000), .eq(comparator_4_eq));  // open: gt, lt
  Comparator #(.width(6), .mode("unsigned")) comparator_5 (
    .a(in_1[5:0]), .b(6'b011010), .eq(comparator_5_eq));  // open: gt, lt
  Comparator #(.width(6), .mode("unsigned")) comparator_6 (.a(in_1[31:26]), .b(6'b000011), .eq(jal));  // open: gt, lt
  Comparator #(.width(6), .mode("unsigned")) comparator_7 (.a(in_1[31:26]), .b(6'b000010), .eq(j));  // open: gt, lt
  Comparator #(.width(6), .mode("unsigned")) comparator_8 (
    .a(in_1[5:0]), .b(6'b001001), .eq(comparator_8_eq));  // open: gt, lt
  Comparator #(.width(6), .mode("unsigned")) comparator_9 (
    .a(in_1[5:0]), .b(6'b001000), .eq(comparator_9_eq));  // open: gt, lt
  or or_1 (Reg_Dst[1], bgezal, jal);
  Comparator #(.width(6), .mode("unsigned")) comparator_10 (
    .a(in_1[5:0]), .b(6'b010011), .eq(comparator_10_eq));  // open: gt, lt
  Comparator #(.width(6), .mode("unsigned")) comparator_11 (
    .a(in_1[5:0]), .b(6'b010000), .eq(comparator_11_eq));  // open: gt, lt
  Comparator #(.width(6), .mode("unsigned")) comparator_12 (
    .a(in_1[5:0]), .b(6'b000011), .eq(comparator_12_eq));  // open: gt, lt
  Comparator #(.width(6), .mode("unsigned")) comparator_13 (.a(in_1[31:26]), .b(6'b000101), .eq(bne));  // open: gt, lt
  Comparator #(.width(6), .mode("unsigned")) comparator_14 (.a(in_1[31:26]), .b(6'b100001), .eq(lh));  // open: gt, lt
  Comparator #(.width(6), .mode("unsigned")) comparator_15 (.a(in_1[31:26]), .b(6'b100101), .eq(lhu));  // open: gt, lt
  Comparator #(.width(6), .mode("unsigned")) comparator_16 (.a(in_1[31:26]), .b(6'b101001), .eq(sh));  // open: gt, lt
  Comparator #(.width(6), .mode("unsigned")) comparator_17 (
    .a(in_1[5:0]), .b(6'b100001), .eq(comparator_17_eq));  // open: gt, lt
  Comparator #(.width(6), .mode("unsigned")) comparator_18 (.a(in_1[31:26]), .b(6'b001000), .eq(addi));  // open: gt, lt
  and and_1 (add, Reg_Dst[0], comparator_2_eq);
  and and_2 (sub, Reg_Dst[0], comparator_3_eq);
  and and_3 (mult, Reg_Dst[0], comparator_4_eq);
  Transistor #(.\type ("n"), .width(5)) transistor_1 (.in(5'b00110), .out(out_5), .gate(div));
  and and_4 (div, Reg_Dst[0], comparator_5_eq);
  and and_5 (jalr, Reg_Dst[0], comparator_8_eq);
  and and_6 (jr, Reg_Dst[0], comparator_9_eq);
  Transistor #(.\type ("n"), .width(5)) transistor_2 (.in(5'b01000), .out(out_5), .gate(mtlo));
  and and_7 (mtlo, Reg_Dst[0], comparator_10_eq);
  Transistor #(.\type ("n"), .width(5)) transistor_3 (.in(5'b01001), .out(out_5), .gate(mfhi));
  and and_8 (mfhi, Reg_Dst[0], comparator_11_eq);
  Transistor #(.\type ("n"), .width(5)) transistor_4 (.in(5'b01011), .out(out_5), .gate(sra));
  and and_9 (sra, Reg_Dst[0], comparator_12_eq);
  Transistor #(.\type ("n"), .width(5)) transistor_5 (.in(5'b00010), .out(out_12), .gate(bne));
  Transistor #(.\type ("n"), .width(5)) transistor_6 (.in({5{1'b0}}), .out(out_5), .gate(lh));
  Transistor #(.\type ("n"), .width(5)) transistor_7 (.in({5{1'b0}}), .out(out_5), .gate(lhu));
  Transistor #(.\type ("n"), .width(5)) transistor_8 (.in({5{1'b0}}), .out(out_5), .gate(sh));
  Transistor #(.\type ("n"), .width(5)) transistor_9 (.in({5{1'b0}}), .out(out_5), .gate(addu));
  and and_10 (addu, Reg_Dst[0], comparator_17_eq);
  Transistor #(.\type ("n"), .width(5)) transistor_10 (.in({5{1'b0}}), .out(out_5), .gate(addi));
  Transistor #(.\type ("n"), .width(5)) transistor_11 (.in({5{1'b0}}), .out(out_5), .gate(add));
  Transistor #(.\type ("n"), .width(5)) transistor_12 (.in(5'b00001), .out(out_5), .gate(sub));
  Transistor #(.\type ("n"), .width(5)) transistor_13 (.in(5'b00101), .out(out_5), .gate(mult));
  or or_2 (jump[0], jal, j);
  or or_3 (jump[1], jalr, jr);
  or or_4 (plus_3000, jal, jalr);
  Comparator #(.width(6), .mode("unsigned")) comparator_19 (
    .a(in_1[5:0]), .b({6{1'b0}}), .eq(comparator_19_eq));  // open: gt, lt
  Comparator #(.width(6), .mode("unsigned")) comparator_20 (
    .a(in_1[5:0]), .b(6'b010001), .eq(comparator_20_eq));  // open: gt, lt
  Comparator #(.width(6), .mode("unsigned")) comparator_21 (
    .a(in_1[5:0]), .b(6'b010010), .eq(comparator_21_eq));  // open: gt, lt
  Comparator #(.width(6), .mode("unsigned")) comparator_22 (
    .a(in_1[5:0]), .b(6'b000010), .eq(comparator_22_eq));  // open: gt, lt
  Comparator #(.width(6), .mode("unsigned")) comparator_23 (.a(in_1[31:26]), .b(6'b100100), .eq(lbu));  // open: gt, lt
  Comparator #(.width(6), .mode("unsigned")) comparator_24 (.a(in_1[31:26]), .b(6'b101000), .eq(sb));  // open: gt, lt
  Comparator #(.width(6), .mode("unsigned")) comparator_25 (.a(in_1[31:26]), .b(6'b100011), .eq(lw));  // open: gt, lt
  Comparator #(.width(6), .mode("unsigned")) comparator_26 (.a(in_1[31:26]), .b(6'b101011), .eq(sw));  // open: gt, lt
  Comparator #(.width(6), .mode("unsigned")) comparator_27 (.a(in_1[31:26]), .b(6'b000100), .eq(beq));  // open: gt, lt
  Comparator #(.width(6), .mode("unsigned")) comparator_28 (
    .a(in_1[31:26]), .b(6'b000001), .eq(comparator_28_eq));  // open: gt, lt
  Comparator #(.width(5), .mode("unsigned")) comparator_29 (
    .a(in_1[20:16]), .b(5'b10001), .eq(comparator_29_eq));  // open: gt, lt
  and and_11 (sll, Reg_Dst[0], comparator_19_eq);
  Comparator #(.width(6), .mode("unsigned")) comparator_30 (.a(in_1[31:26]), .b(6'b001101), .eq(ori));  // open: gt, lt
  Comparator #(.width(6), .mode("unsigned")) comparator_31 (.a(in_1[31:26]), .b(6'b001111), .eq(lui));  // open: gt, lt
  Comparator #(.width(6), .mode("unsigned")) comparator_32 (
    .a(in_1[31:26]), .b(6'b001001), .eq(addiu));  // open: gt, lt
  or or_5 (I_type, ori, lui, addiu, addi);
  and and_12 (srl, Reg_Dst[0], comparator_22_eq);
  Transistor #(.\type ("n"), .width(5)) transistor_14 (.in({5{1'b0}}), .out(out_5), .gate(lb));
  Comparator #(.width(6), .mode("unsigned")) comparator_33 (.a(in_1[31:26]), .b(6'b100000), .eq(lb));  // open: gt, lt
  Transistor #(.\type ("n"), .width(5)) transistor_15 (.in({5{1'b0}}), .out(out_5), .gate(lbu));
  Transistor #(.\type ("n"), .width(5)) transistor_16 (.in({5{1'b0}}), .out(out_5), .gate(sb));
  or or_6 (D2R[0], lbu, lb, lw, lh, lhu);
  or or_7 (write, sh, sw, sb);
  Transistor #(.\type ("n"), .width(5)) transistor_17 (.in({5{1'b0}}), .out(out_5), .gate(lw));
  Transistor #(.\type ("n"), .width(5)) transistor_18 (.in({5{1'b0}}), .out(out_5), .gate(sw));
  Transistor #(.\type ("n"), .width(5)) transistor_19 (.in({5{1'b0}}), .out(out_12), .gate(beq));
  Transistor #(.\type ("n"), .width(5)) transistor_20 (.in(5'b00001), .out(out_12), .gate(bgezal));
  and and_13 (bgezal, comparator_28_eq, comparator_29_eq);
  Transistor #(.\type ("n"), .width(5)) transistor_21 (.in(5'b00100), .out(out_5), .gate(sll));
  Transistor #(.\type ("n"), .width(5)) transistor_22 (.in(5'b00010), .out(out_5), .gate(ori));
  Transistor #(.\type ("n"), .width(5)) transistor_23 (.in(5'b00011), .out(out_5), .gate(lui));
  Transistor #(.\type ("n"), .width(5)) transistor_24 (.in({5{1'b0}}), .out(out_5), .gate(addiu));
  Transistor #(.\type ("n"), .width(5)) transistor_25 (.in(5'b00111), .out(out_5), .gate(mthi));
  and and_14 (mthi, Reg_Dst[0], comparator_20_eq);
  Transistor #(.\type ("n"), .width(5)) transistor_26 (.in(5'b01010), .out(out_5), .gate(mflo));
  and and_15 (mflo, Reg_Dst[0], comparator_21_eq);
  Transistor #(.\type ("n"), .width(5)) transistor_27 (.in(5'b01100), .out(out_5), .gate(srl));
  or or_8 (width_op[0], lh, lhu, sh);
  or or_9 (width_op[1], lb, lbu, sb);
  or or_10 (D2R[1], jalr, Reg_Dst[1]);
  buf or_11 (compareWrite, bgezal);  // OR_Gate
  or or_12 (shamt, sra, srl, sll);
  buf or_13 (MemWrite, write);  // OR_Gate
  or or_14 (Branch, beq, bgezal, bne);
  or or_15 (ALUsrcB, I_type, write, D2R[0]);
  or or_16 (RegWrite, bgezal, Reg_Dst[0], I_type, D2R[0], plus_3000);
  buf or_17 (ALU_srcA, shamt);  // OR_Gate
  buf or_18 (imm_ext, ori);  // OR_Gate
  or or_19 (sign_0, lhu, lbu);

  // Other names for the same wires on the sheet: ALU_op[4:0] = out_5; Com_op[4:0] = out_12; load = D2R[0];
  //   funct[5:0] = in_1[5:0]; Instr[31:0] = in_1; rt[4:0] = in_1[20:16]; op[5:0] = in_1[31:26]; J_write = plus_3000;
  //   Jump1 = jump[0]; Jump2 = jump[1]; R_type = Reg_Dst[0]; ra = Reg_Dst[1]; half = width_op[0]; byte = width_op[1]

  // Notes on the sheet:
  //   1.R_type_calculate
  //   7.Jump
  //   改
  //   2.I_type
  //   3.Load
  //   4.Write
  //   5.Branch
  //   6.R_shamt
  //   是否等于0
  //   是否大于等于0
  //   改
  //   改
  //   改
  //   PC+4
endmodule

module ALU (
  input  [4:0] ALU_control,
  input  [31:0] in_2,
  input  [31:0] in_3,
  input  in_4,
  input  in_5,
  output [31:0] out_6
);

  wire div_en, HI_en, LO_en, mfhi_en, mflo_en, mthi_en, mtlo_en, mult_en;
  wire [31:0] add, \and , divider_1_out, divider_1_rem, HI, LO, multiplier_1_cout, multiplier_1_out, \or ,
       sll, sra, srl, sub, transistor_1_out, transistor_2_out;

  Adder #(.width(32)) adder_1 (.a(in_2), .b(in_3), .out(add));  // open: cin, cout
  assign \or  = in_2 | in_3;  // OR_Gate or_1, 32 bits wide
  Subtractor #(.width(32)) subtractor_1 (.a(in_2), .b(in_3), .out(sub));  // open: bin, bout
  assign \and  = in_2 & in_3;  // AND_Gate and_1, 32 bits wide
  Shifter #(.width(32)) shifter_1 (.in(in_3), .\dist (in_2[4:0]), .out(sll));
  Multiplier #(.width(32)) multiplier_1 (
    .a(in_2), .b(in_3), .out(multiplier_1_out), .cout(multiplier_1_cout));  // open: cin
  Divider #(.width(32)) divider_1 (.a(in_2), .b(in_3), .out(divider_1_out), .rem(divider_1_rem));  // open: upper
  Transistor #(.\type ("n"), .width(32)) transistor_1 (.in(multiplier_1_out), .out(transistor_1_out), .gate(mult_en));
  Transistor #(.\type ("n"), .width(32)) transistor_2 (.in(multiplier_1_cout), .out(transistor_2_out), .gate(mult_en));
  Transistor #(.\type ("n"), .width(32)) transistor_3 (.in(divider_1_out), .out(transistor_1_out), .gate(div_en));
  Transistor #(.\type ("n"), .width(32)) transistor_4 (.in(divider_1_rem), .out(transistor_2_out), .gate(div_en));
  Transistor #(.\type ("n"), .width(32)) transistor_5 (.in(in_2), .out(transistor_1_out), .gate(mtlo_en));
  Transistor #(.\type ("n"), .width(32)) transistor_6 (.in(in_2), .out(transistor_2_out), .gate(mthi_en));
  Shifter #(.width(32), .shift("ar")) shifter_2 (.in(in_3), .\dist (in_2[4:0]), .out(sra));
  Shifter #(.width(32), .shift("lr")) shifter_3 (.in(in_3), .\dist (in_2[4:0]), .out(srl));
  Register #(.width(32)) u_HI (.D(transistor_2_out), .en(HI_en), .Q(HI), .clk(in_4), .clr(in_5));
  Register #(.width(32)) u_LO (.D(transistor_1_out), .en(LO_en), .Q(LO), .clk(in_4), .clr(in_5));
  Comparator #(.width(5), .mode("unsigned")) comparator_1 (
    .a(ALU_control), .b(5'b00101), .eq(mult_en));  // open: gt, lt
  Comparator #(.width(5), .mode("unsigned")) comparator_2 (.a(ALU_control), .b(5'b00110), .eq(div_en));  // open: gt, lt
  Comparator #(.width(5), .mode("unsigned")) comparator_3 (
    .a(ALU_control), .b(5'b00111), .eq(mthi_en));  // open: gt, lt
  or or_2 (HI_en, mult_en, mthi_en, div_en);
  or or_3 (LO_en, mtlo_en, mult_en, div_en);
  Multiplexer #(.select(5), .width(32)) multiplexer_1 (
    .in0(add), .in1(sub), .in2(\or ), .in3({in_3[15:0], {16{1'b0}}}), .in4(sll), .in9(HI), .in10(LO),
    .in11(sra), .out(out_6), .sel(ALU_control));  // open: in5, in6, in7, in8, in12, in13, in14, in15, in16, in17, in18, in19, in20, in21, in22, in23, in24, in25, in26, in27, in28, in29, in30, in31, en
  Comparator #(.width(5), .mode("unsigned")) comparator_4 (
    .a(ALU_control), .b(5'b01000), .eq(mtlo_en));  // open: gt, lt
  Comparator #(.width(5), .mode("unsigned")) comparator_5 (
    .a(ALU_control), .b(5'b01001), .eq(mfhi_en));  // open: gt, lt
  Comparator #(.width(5), .mode("unsigned")) comparator_6 (
    .a(ALU_control), .b(5'b01010), .eq(mflo_en));  // open: gt, lt

  // Other names for the same wires on the sheet: clk = in_4; lui[31:16] = in_3[15:0]; srcB[31:0] = in_3; reset = in_5;
  //   srcA[31:0] = in_2
endmodule

module Compare (
  input  [31:0] in_1,
  input  [31:0] in_2,
  input  [4:0] com_op,
  output out_4
);

  wire beq, bgez, bne, comparator_1_eq, comparator_2_gt, comparator_4_gt, comparator_4_lt;
  wire [31:0] subtractor_1_out, subtractor_2_out;

  Subtractor #(.width(32)) subtractor_1 (.a(in_1), .b(in_2), .out(subtractor_1_out));  // open: bin, bout
  Comparator #(.width(32), .mode("unsigned")) comparator_1 (
    .a(in_1), .b({32{1'b0}}), .eq(comparator_1_eq));  // open: gt, lt
  Comparator #(.width(32)) comparator_2 (.a(in_1), .b({32{1'b0}}), .gt(comparator_2_gt));  // open: eq, lt
  Subtractor #(.width(32)) subtractor_2 (.a(in_1), .b(in_2), .out(subtractor_2_out));  // open: bin, bout
  Comparator #(.width(32), .mode("unsigned")) comparator_3 (
    .a(subtractor_1_out), .b({32{1'b0}}), .eq(beq));  // open: gt, lt
  Comparator #(.width(32), .mode("unsigned")) comparator_4 (
    .a(subtractor_2_out), .b({32{1'b0}}), .gt(comparator_4_gt), .lt(comparator_4_lt));  // open: eq
  or or_1 (bgez, comparator_1_eq, comparator_2_gt);
  or or_2 (bne, comparator_4_gt, comparator_4_lt);
  Multiplexer #(.select(5)) multiplexer_1 (
    .in0(beq), .in1(bgez), .in2(bne), .out(out_4), .sel(com_op));  // open: in3, in4, in5, in6, in7, in8, in9, in10, in11, in12, in13, in14, in15, in16, in17, in18, in19, in20, in21, in22, in23, in24, in25, in26, in27, in28, in29, in30, in31, en

  // Other names for the same wires on the sheet: srcA[31:0] = in_1; srcB[31:0] = in_2
endmodule

module DM_write (
  input  [31:0] DM_data,
  input  [31:0] in_2,
  input  [1:0] op,
  input  [31:0] Address,
  output [31:0] out_5
);

  wire [7:0] Byte;
  wire [15:0] half;

  Multiplexer #(.select(2), .width(8)) multiplexer_1 (
    .in0(in_2[7:0]), .in1(in_2[15:8]), .in2(in_2[23:16]), .in3(in_2[31:24]), .out(Byte), .sel(Address[1:0]));  // open: en
  Multiplexer #(.width(16)) multiplexer_2 (
    .in0(in_2[15:0]), .in1(in_2[31:16]), .out(half), .sel(Address[1]));  // open: en
  Multiplexer #(.select(2), .width(32)) multiplexer_3 (
    .in0(in_2), .in1({DM_data[31:16], half}), .in2({DM_data[31:8], Byte}), .out(out_5), .sel(op));  // open: in3, en

  // Other names for the same wires on the sheet: _2_bits_op[1:0] = Address[1:0]; _1_bit_op = Address[1];
  //   Byte[31:8] = DM_data[31:8]; group2[7:0] = DM_data[15:8]; group3[7:0] = DM_data[23:16];
  //   half[31:16] = DM_data[31:16]; group4[7:0] = DM_data[31:24]; group1[7:0] = DM_data[7:0];
  //   cluster1[15:0] = in_2[15:0]; word[31:0] = in_2; write1[7:0] = in_2[7:0]; write2[7:0] = in_2[15:8];
  //   cluster2[15:0] = in_2[31:16]; write3[7:0] = in_2[23:16]; write4[7:0] = in_2[31:24]
endmodule

module DM_read (
  input  [31:0] MemData,
  input  [31:0] Address,
  input  sign_zero,
  input  [1:0] width_op,
  output [31:0] out_5
);

  wire [7:0] multiplexer_1_out;
  wire [15:0] multiplexer_2_out;
  wire [31:0] bit_extender_1_out, bit_extender_2_out, bit_extender_3_out, bit_extender_4_out, byte_read,
       half_read;

  Multiplexer #(.select(2), .width(8)) multiplexer_1 (
    .in0(MemData[7:0]), .in1(MemData[15:8]), .in2(MemData[23:16]), .in3(MemData[31:24]),
    .out(multiplexer_1_out), .sel(Address[1:0]));  // open: en
  Multiplexer #(.width(16)) multiplexer_2 (
    .in0(MemData[15:0]), .in1(MemData[31:16]), .out(multiplexer_2_out), .sel(Address[1]));  // open: en
  assign bit_extender_1_out = {{24{multiplexer_1_out[7]}}, multiplexer_1_out};  // Bit_Extender bit_extender_1
  assign bit_extender_2_out = {{24{1'b0}}, multiplexer_1_out};  // Bit_Extender bit_extender_2
  assign bit_extender_3_out = {{16{multiplexer_2_out[15]}}, multiplexer_2_out};  // Bit_Extender bit_extender_3
  assign bit_extender_4_out = {{16{1'b0}}, multiplexer_2_out};  // Bit_Extender bit_extender_4
  Multiplexer #(.select(2), .width(32)) multiplexer_3 (
    .in0(MemData), .in1(half_read), .in2(byte_read), .out(out_5), .sel(width_op));  // open: in3, en
  Multiplexer #(.width(32)) multiplexer_4 (
    .in0(bit_extender_1_out), .in1(bit_extender_2_out), .out(byte_read), .sel(sign_zero));  // open: en
  Multiplexer #(.width(32)) multiplexer_5 (
    .in0(bit_extender_3_out), .in1(bit_extender_4_out), .out(half_read), .sel(sign_zero));  // open: en

  // Other names for the same wires on the sheet: _2_bits_op[1:0] = Address[1:0]; _1_bit_op = Address[1];
  //   data_op[1:0] = width_op; cluster1[15:0] = MemData[15:0]; group1[7:0] = MemData[7:0]; word_read[31:0] = MemData;
  //   group2[7:0] = MemData[15:8]; cluster2[15:0] = MemData[31:16]; group3[7:0] = MemData[23:16];
  //   group4[7:0] = MemData[31:24]
endmodule
